// Logisim project Multiplier-4bit-by-3bit.circ as structural Verilog: 1 circuit, main circuit main
module main (
  input  B0,
  input  B1,
  input  B2,
  input  B3,
  input  A0,
  input  A1,
  input  A2,
  input  in_8
);

  wire adder_2_cout, and_11_out;
  wire [0:0] adder_1_out_2;
  wire [2:0] and_12_out;
  wire [3:0] adder_1_out, adder_2_out, and_4_out, and_8_out;

  and and_1 (and_4_out[3], A2, B3);
  and and_2 (and_4_out[2], A2, B2);
  and and_3 (and_4_out[1], A2, B1);
  and and_4 (and_4_out[0], A2, B0);
  and and_5 (and_8_out[3], A1, B3);
  and and_6 (and_8_out[1], A1, B1);
  and and_7 (and_8_out[2], A1, B2);
  and and_8 (and_8_out[0], A1, B0);
  and and_9 (and_12_out[2], A0, B3);
  and and_10 (and_12_out[1], A0, B2);
  and and_11 (and_11_out, A0, B0);
  and and_12 (and_12_out[0], A0, B1);
  Adder #(.width(4)) adder_1 (
    .a({in_8, and_12_out}), .b(and_8_out), .out({adder_1_out[2:0], adder_1_out_2[0]}), .cout(adder_1_out[3]));  // open: cin
  Adder #(.width(4)) adder_2 (.a(adder_1_out), .b(and_4_out), .out(adder_2_out), .cout(adder_2_cout));  // open: cin
  LED led_1 (.in(and_11_out));
  LED led_2 (.in(adder_1_out_2[0]));
  LED led_3 (.in(adder_2_out[0]));
  LED led_4 (.in(adder_2_out[1]));
  LED led_5 (.in(adder_2_out[2]));
  LED led_6 (.in(adder_2_out[3]));
  LED led_7 (.in(adder_2_cout));

  // Notes on the sheet:
  //   p0
  //   p1
  //   p2
  //   p3
  //   p4
  //   p5
  //   p6
endmodule
